// Logisim project 8 bit register.circ as structural Verilog
module _8_bit_register (
  input  in_1,
  input  in_2,
  input  in_3,
  input  in_4,
  input  in_5,
  input  in_6,
  input  in_7,
  output out_8,
  output out_9,
  output out_10,
  output out_11,
  output out_12,
  output out_13,
  output out_14
);

  wire button_1_out, clock_1_out;

  Clock clock_1 (.out(clock_1_out));
  Button button_1 (.out(button_1_out));
  D_Flip_Flop d_ff_1 (.clk(clock_1_out), .D(in_7), .Q(out_9), .en(button_1_out));  // open: Qn, preset, reset
  D_Flip_Flop d_ff_2 (.clk(clock_1_out), .D(in_6), .Q(out_10), .en(button_1_out));  // open: Qn, preset, reset
  D_Flip_Flop d_ff_3 (.clk(clock_1_out), .D(in_2), .Q(out_11), .en(button_1_out));  // open: Qn, preset, reset
  D_Flip_Flop d_ff_4 (.clk(clock_1_out), .D(in_3), .Q(out_12), .en(button_1_out));  // open: Qn, preset, reset
  D_Flip_Flop d_ff_5 (.clk(clock_1_out), .D(in_4), .Q(out_13), .en(button_1_out));  // open: Qn, preset, reset
  D_Flip_Flop d_ff_6 (.clk(clock_1_out), .D(in_5), .Q(out_14), .en(button_1_out));  // open: Qn, preset, reset
  D_Flip_Flop d_ff_7 (.clk(clock_1_out), .D(in_1), .Q(out_8), .en(button_1_out));  // open: Qn, preset, reset
endmodule
